# Fritzing sketch HC08 (saved by Fritzing 0.9.9b)
circuit board: 14.1475cm x 5.69692cm

parts:
  Componente1 = Arduino Uno (Rev3)
  Componente2 = Bluetooth HC-05 Macho

nets:
  N1: Componente1.D2, Componente2.TXD
  N2: Componente1.D3_PWM, Componente2.RXD
  5V: Componente1.5V, Componente2.VCC
  GND: Componente1.GND, Componente2.GND

notes:
  Foi usado o componente HC-05 apenas para representar o esquema de conexões. JAMAIS LIGAR O HC-05 DIRETO. Para esse componente é necessário um adaptador de nivel lógico.
